# Fritzing sketch BT_temp_humidity_SD_RTC_mega (saved by Fritzing 0.7.11b)
breadboards: 1

parts:
  DHT1 = DHT22 Humidity and Temperature Sensor
  microSD1 = MicroSD Breakout
  RTC1 = DS1307 RTC Breakout
  R2 = Trimmer Potentiometer [maximum_resistance=10kΩ package=THT]
  LCD1 = LCD screen
  U1 = Arduino Mega
  R1 = 10k Ω Resistor [package=THT]
  BT_HC-05_1 = Bluetooth HC-05

nets:
  5V: DHT1.VDD, microSD1.5V, RTC1.5V, R2.leg1, LCD1.VDD, LCD1.LED+, U1.+5V, R1.Pin_0, BT_HC-05_1.5V
  N1: DHT1.DATA, U1.D10, R1.Pin_1
  GND: DHT1.GND, microSD1.GND, microSD1.3v, RTC1.GND, R2.leg2, LCD1.VSS, LCD1.R/W, LCD1.LED-, U1.GND, BT_HC-05_1.GND
  N2: microSD1.CS, U1.D9
  N3: microSD1.DI, U1.D51
  N4: microSD1.DO, U1.D50
  N5: microSD1.CLK, U1.D52
  N6: RTC1.SDA, U1.D20
  N7: RTC1.SCL, U1.D21
  N8: R2.wiper, LCD1.V0
  N9: LCD1.RS, U1.D7
  N10: LCD1.E, U1.D6
  N11: LCD1.DB4, U1.D5
  N12: LCD1.DB5, U1.D4
  N13: LCD1.DB6, U1.D3
  N14: LCD1.DB7, U1.D2
  N15: U1.D14, BT_HC-05_1.RX
  N16: U1.D15, BT_HC-05_1.TX

custom parts:
  MicroSD Breakout: 5V-ready microSD Breakout with Level Shifter
  DS1307 RTC Breakout: DS1307 Real-time Clock Breakout Board with Battery
  Bluetooth HC-05: Bluetooth HC-05 serial adapter
